# Fritzing sketch ArduinoSiren (saved by Fritzing 0.9.3b)
circuit board: 16.5266cm x 3.18017cm
breadboards: 1

parts:
  LED1 = LED - 5mm [color="Red (633nm)" package="5 mm [THT]"]
  LED2 = LED - 5mm [color="Red (633nm)" package="5 mm [THT]"]
  LED3 = LED - 5mm [color="Red (633nm)" package="5 mm [THT]"]
  LED4 = LED - 5mm [color="Red (633nm)" package="5 mm [THT]"]
  LED5 = LED - 5mm [color="Red (633nm)" package="5 mm [THT]"]
  LED6 = LED - 5mm [color="Blue (430nm)" package="5 mm [THT]"]
  LED7 = LED - 5mm [color="Blue (430nm)" package="5 mm [THT]"]
  LED8 = LED - 5mm [color="Blue (430nm)" package="5 mm [THT]"]
  LED9 = LED - 5mm [color="Blue (430nm)" package="5 mm [THT]"]
  LED10 = LED - 5mm [color="Blue (430nm)" package="5 mm [THT]"]
  S1 = Momentary Switch [package=ksa_sealed_tac_switch]
  S2 = Momentary Switch [package=ksa_sealed_tac_switch]
  VCC1 = Battery block 9V
  C1 = Capacitor Polarized [package=cpol-radial-10uf-25v]
  C2 = Capacitor Polarized [package=cpol-radial-10uf-25v]
  ATMEGA328P = atmega328 [package=dip]
  R12 = Resistor [tolerance=±5% resistance=10k package=THT]
  R1 = Resistor [tolerance=±5% resistance=220 package=THT]
  R7 = Resistor [tolerance=±5% resistance=220 package=THT]
  R3 = Resistor [tolerance=±5% resistance=220 package=THT]
  R4 = Resistor [tolerance=±5% resistance=220 package=THT]
  R5 = Resistor [tolerance=±5% resistance=220 package=THT]
  R10 = Resistor [tolerance=±5% resistance=220 package=THT]
  R9 = Resistor [tolerance=±5% resistance=220 package=THT]
  R8 = Resistor [tolerance=±5% resistance=220 package=THT]
  R6 = Resistor [tolerance=±5% resistance=220 package=THT]
  R2 = Resistor [tolerance=±5% resistance=220 package=THT]
  XTAL1 = Crystal [frequency="16 Mhz" package=THT]
  C4 = Ceramic Capacitor [capacitance=22pF package="0805 [SMD, multilayer]"]
  C3 = Ceramic Capacitor [capacitance=22pF package="0805 [SMD, multilayer]"]
  LED11 = LED - 5mm [color="Green (555nm)" package="5 mm [THT]"]
  R23 = Resistor [tolerance=±5% resistance=220 package=THT]
  J2 = Piezo Speaker
  R11 = Resistor [tolerance=±5% resistance=100 package=THT]
  R12_2 = Resistor [tolerance=±5% resistance=10k package=THT]
  J1 = Voltage Regulator - 5V [package="TO220 [THT]"]
  S4 = Toggle Switch [package=THT]

nets:
  N1: LED1.cathode, R1.Pin_0
  N2: LED1.anode, ATMEGA328P.D3_(PWM)
  N3: LED2.cathode, R2.Pin_0
  N4: LED2.anode, ATMEGA328P.D4
  N5: LED3.cathode, R3.Pin_0
  N6: LED3.anode, ATMEGA328P.D5_(PWM)
  N7: LED4.cathode, R4.Pin_0
  N8: LED4.anode, ATMEGA328P.D6_(PWM)
  N9: LED5.cathode, R5.Pin_0
  N10: LED5.anode, ATMEGA328P.D7
  N11: LED6.cathode, R6.Pin_0
  N12: LED6.anode, ATMEGA328P.D11_(PWM)
  N13: LED7.cathode, R7.Pin_0
  N14: LED7.anode, ATMEGA328P.D12
  N15: LED8.cathode, R8.Pin_0
  N16: LED8.anode, ATMEGA328P.D10_(PWM)
  N17: LED9.cathode, R9.Pin_0
  N18: LED9.anode, ATMEGA328P.D9_(PWM)
  N19: LED10.cathode, R10.Pin_0
  N20: LED10.anode, ATMEGA328P.D8
  N21: S1.2, C1.+, ATMEGA328P.VCC, ATMEGA328P.AVCC, ATMEGA328P.AREF, R12.Pin_0, LED11.anode, J1.output_voltage
  N22: S1.3, R12_2.Pin_0
  N23: S1.4, ATMEGA328P.D2
  N24: S2.2, ATMEGA328P.RESET, R12.Pin_1
  GND: S2.4, VCC1.-, C1.-, C2.-, ATMEGA328P.GND, R1.Pin_1, R7.Pin_1, R3.Pin_1, R4.Pin_1, R5.Pin_1, R10.Pin_1, R9.Pin_1, R8.Pin_1, R6.Pin_1, R2.Pin_1, C4.0, C3.0, R23.Pin_1, R11.Pin_1, R12_2.Pin_1, J1.GND, S4.L1
  N25: VCC1.+, C2.+, J1.input_voltage, S4.COM
  N26: ATMEGA328P.XLAT1, XTAL1.pin_0, C4.1
  N27: ATMEGA328P.XLAT2, XTAL1.pin_1, C3.1
  N28: ATMEGA328P.D13, J2.pin2
  N29: LED11.cathode, R23.Pin_0
  N30: J2.pin1, R11.Pin_0
